# Fritzing sketch Greenhouse System (saved by Fritzing 1.0.5)
breadboards: 1

parts:
  IR1 = vs1838b [package=THT]
  Part1 = Arduino Uno (Rev3) - ICSP
  DHT1 = DHT11 Humitidy and Temperature Sensor (3 pins)
  Part2 = FC-28 Soil Hygrometer Module
  Part3 = FC-28 Soil Hygrometer Module - Probe
  LCM1602_IIC1 = LCM1602 IIC [part_number="LCM1602 IIC" chip_label="LCM1602 IIC" package="DIP (Dual Inline) [THT]"]
  U1 = LCD-16X2 [package=lcd-16x2]
  Mod1 = KY-019 5V Relay Module [package="Breakout board"]
  WATER_PUMP1 = water pump/motor
  M1 = water level switch

nets:
  GND: IR1.GND, Part1.GND, DHT1.Gnd, Part2.GND, Mod1.-, M1.pin2
  N1: IR1.Vs, Part1.D4
  5V: IR1.Data, Part1.5V, DHT1.Signal, Part2.VCC, Mod1.+
  N2: Part1.A0, Part2.DO
  N3: Part1.A4/SDA, LCM1602_IIC1.SDA
  N4: Part1.A5/SCL, LCM1602_IIC1.SCL
  N5: Part1.D2, DHT1.Plus
  N6: Part1.D3_PWM, Mod1.S
  N7: Part1.D5_PWM, M1.pin1
  N8: Part2.POS, Part3.POS
  N9: Part2.NEG, Part3.NEG
  VSS: LCM1602_IIC1.VSS, U1.VSS
  VDD: LCM1602_IIC1.VDD, U1.VDD
  N10: LCM1602_IIC1.V0, U1.VO
  N11: LCM1602_IIC1.RS, U1.RS
  N12: LCM1602_IIC1.RW, U1.R_W
  N13: LCM1602_IIC1.E, U1.E
  N14: LCM1602_IIC1.D0, U1.DB0
  N15: LCM1602_IIC1.D1, U1.DB1
  N16: LCM1602_IIC1.D2, U1.DB2
  N17: LCM1602_IIC1.D3, U1.DB3
  N18: LCM1602_IIC1.D4, U1.DB4
  N19: LCM1602_IIC1.D5, U1.DB5
  N20: LCM1602_IIC1.D6, U1.DB6
  N21: LCM1602_IIC1.D7, U1.DB7
  N22: LCM1602_IIC1.A, U1.A
  N23: LCM1602_IIC1.K, U1.K
  N24: LCM1602_IIC1.LED_A, LCM1602_IIC1.LED_B
  N25: Mod1.Common, WATER_PUMP1.pin_2
  N26: Mod1.NO, WATER_PUMP1.pin_1

custom parts:
  DHT11 Humitidy and Temperature Sensor (3 pins): DHT11 Humidity and Temperature Sensor (3 pins).
  FC-28 Soil Hygrometer Module: The FC-28 is a soil hygrometer module that uses the Texas Instruments LM393 comparator chip to provide an analog measurement of soil humidity. The digital output is high when soil moisture is over a certain threshold, as determined by adjusting the potentiometer.
  FC-28 Soil Hygrometer Module - Probe: The FC-28 is a soil hygrometer module that uses the Texas Instruments LM393 comparator chip to provide an analog measurement of soil humidity.
  LCM1602 IIC: I2C-Module to use a 1602 or 2004 LCD on with the wire.h libory Serial LCD Modul
  KY-019 5V Relay Module: KY-019 5V Relay module, used to control AC circuits. (Special thanks to vanepp for fixing the PCB holes and other errors)
  water pump/motor: WATER PUMP BY ARDUBLOCKTR
  water level switch: Generic water level float switch.

// code stored in the sketch: Main.ino
//Greenhouse Management System by Aidan Makumbe RT 

#include <IRremote.h> // Responsible for interfacing with the IR Sensor VS1838B
#include "DHT.h" //Interfacing with Temperature and Humidity Sensor DHT11
#include <LiquidCrystal_I2C.h>//For interfacing with the LCD

//Defining pins and Variables
#define DHT_TYPE DHT11
const int DHT_PIN = 2;
const int RELAY_PIN = 3;
const int WATER_SENSOR_PIN = 5;  // Float switch pin
const int moistureSensor = A0;
const unsigned long BUTTON_CODE = 0x202F1329; //Put Activation code here 

const float maximumMoistureLevel = 156;
float currentMoistureLevel;
float moisture;
String state = ""; 



bool relayState = false;
bool waterOK = false;

const int RECV_PIN = 4;  // IR receiver data pin connected to D2
IRrecv irrecv(RECV_PIN);
decode_results results;
DHT dht(DHT_PIN, DHT_TYPE);
LiquidCrystal_I2C lcd(0x3F, 16, 2);


byte emptyDroplet[8] = {
  B00100,  //    ▓
  B00100,  //    ▓
  B01010,  //  ▓   ▓
  B10001,  // ▓     ▓
  B10001,  // ▓     ▓
  B10001,  // ▓     ▓
  B01110,  //   ▓▓▓   Empty 
  B00000   //
};

byte lowDroplet[8] = {
  B00100,  //    ▓
  B00100,  //    ▓
  B01010,  //   ▓ ▓
  B10001,  //  ▓   ▓
  B10001,  // ▓     ▓
  B10001,  // ▓     ▓
  B01110,  //   ▓▓▓
  B00100   //    ▓    Small low fill
};

byte mediumDroplet[8] = {
  B00100,  //   ▓
  B00100,  //   ▓
  B01010,  // ▓   ▓
  B10001,  //▓     ▓
  B10001,  //▓▓▓▓▓▓▓
  B01110,  // ▓▓▓▓▓ 
  B01110,  //   ▓     Mid fill line
  B00100
};

byte fullDroplet[8] = {
  B00100, //      ▓   
  B00100, //      ▓       
  B01110, //    ▓▓▓▓▓   
  B11111, //   ▓▓▓▓▓▓▓ 
  B11111, //  ▓▓▓▓▓▓▓▓▓
  B11111, //   ▓▓▓▓▓▓▓
  B01110, //    ▓▓▓▓▓
  B00100  //      ▓   Full Fill
};

void setup(){
  // Configuring I/O pins
  pinMode(moistureSensor, INPUT);
  pinMode( RELAY_PIN, OUTPUT);
  digitalWrite(RELAY_PIN, LOW);
  pinMode(WATER_SENSOR_PIN, INPUT_PULLUP); // Internal pull-up, active LOW



  // Starting up Essential Services
  Serial.begin(9600);
  dht.begin(); // Starting DHT services
  irrecv.enableIRIn(); // Enable IR Reciever

  // Initialize LCD
  lcd.init();         
  lcd.backlight();

  // Create custom characters in CGRAM (slots 0–3)
  lcd.createChar(0, emptyDroplet);
  lcd.createChar(1, lowDroplet);
  lcd.createChar(2, mediumDroplet);
  lcd.createChar(3, fullDroplet);
  
  lcd.setCursor(5, 0);
  lcd.print("Welcome");
  lcd.setCursor(7, 1);
  lcd.print("To");
  delay(2000);
  lcd.clear();

  lcd.setCursor(5, 0);
  lcd.print("Greenhouse");
  lcd.setCursor(3, 1);
  lcd.print("System");
  delay(2000);
  lcd.clear();

}
void waterplant(){

    if (waterOK) {
      relayState = !relayState;
      //digitalWrite(RELAY_PIN, relayState ? HIGH : LOW);
        //Activate Relay
      digitalWrite(RELAY_PIN, HIGH);

      lcd.clear();
      lcd.setCursor(0,0);
      lcd.print("Watering.");
      delay(1000);
      lcd.setCursor(0,0);
      lcd.print("Watering..");
      delay(1000);
      lcd.setCursor(0,0);
      lcd.print("Watering...");
      delay(2000);

      digitalWrite(RELAY_PIN, LOW);
      lcd.clear();
        //Serial.println(relayState ? "Relay ON" : "Relay OFF");
      } else {
        lcd.clear();
        lcd.setCursor(0,0);
        lcd.print("Cannot water...");
        lcd.setCursor(0,1);
        lcd.print("Water level low!");
        delay(3500);
        lcd.clear();
      }

}

void loop(){
  int temp = dht.readTemperature();
  int hum = dht.readHumidity();

  currentMoistureLevel = analogRead(moistureSensor);
  moisture = currentMoistureLevel / maximumMoistureLevel;
  
  waterOK = digitalRead(WATER_SENSOR_PIN) == LOW; // LOW = water present

  if(digitalRead(WATER_SENSOR_PIN) == LOW){
    waterOK = true;
    state = "F";
  }
  else{
    waterOK = false;
    state = "E";
  }

  if( moisture <= 0.1){
    //  Execute if the Moisture is below 10%
    lcd.setCursor(9,0);
    lcd.write(byte(0)); //Special Character for moisture 
    waterplant();
  }
  else if( moisture <= 0.3 && moisture >0.1 ){
    // Execute if the Moisture is between 10% and 30%
    lcd.setCursor(9,0);
    lcd.write(byte(1)); //Special Character for moisture 
    waterplant();
  }
  else if(moisture <= 0.6 && moisture > 0.3){
    // Execute if the Moisture is between 30% and 60%
    lcd.setCursor(9,0);
    lcd.write(byte(2)); //Special Character for moisture 
  }
  else{
    // Otherwise the moisture level is above 60% and therefore its good enough
    lcd.setCursor(9,0);
    lcd.write(byte(3)); //Special Character for moisture 
  }

  if (irrecv.decode(&results)) {
    if(results.value == BUTTON_CODE){
      waterplant();
    }
    irrecv.resume();  // Receive the next value
  }
  //Refreshing the LCD input
  
  //Row 1
  lcd.setCursor(0,0);
  lcd.print("Moist:");
  lcd.print(round(moisture*100));
  lcd.print("%");
  lcd.setCursor(11,0);
  lcd.print("Lvl:");
  lcd.print(state);


  //Row 2 of LCD
  lcd.setCursor(8,1);
  lcd.print("Temp:");
  lcd.print(temp);
  lcd.print("C");
  lcd.setCursor(0,1);
  lcd.print("Hum:");
  lcd.print(hum);
  lcd.print("%");


  //Output to Serial
  Serial.print("Temp: ");
  Serial.print(temp);
  Serial.print(" ˚C | Humidity: ");
  Serial.print(hum);
  Serial.print(" % |");
  Serial.print(" Moisture: ");
  Serial.print(moisture*100);
  Serial.print("% |");
  Serial.print(" Water level: ");
  Serial.println(state);
  delay(2000);

}

// code stored in the sketch: Untitled2.ino
#include <IRremote.h>
